# Fritzing sketch Schematic TwoLight Arduino Nano v3 (saved by Fritzing 0.9.4)
breadboards: 1

parts:
  M1 = LM393 Light Sensor [package=THT]
  M2 = LM393 Light Sensor [package=THT]
  LED1 = smd LED [color="Red (633nm)" package="1206 [SMD]"]
  LED2 = smd LED [color="Red (633nm)" package="1206 [SMD]"]
  R2 = Resistor [tolerance=±5% resistance=220 package=THT]
  R3 = Resistor [tolerance=±5% resistance=220 package=THT]
  R4 = Resistor [tolerance=±5% resistance=10M package=THT]
  R5 = Resistor [tolerance=±5% resistance=10M package=THT]
  Part1 = Arduino Nano (Rev3.0)

nets:
  N1: M1.pin1, R4.Pin_1, Part1.D2, Part1.D3
  N2: M1.pin2, M2.pin2, R2.Pin_1, R3.Pin_1, Part1.GND
  N3: M1.pin3, M2.pin3, R4.Pin_0, R5.Pin_0, Part1.5V
  N4: M2.pin1, R5.Pin_1, Part1.D4
  N5: LED1.cathode, R3.Pin_0
  N6: LED1.anode, Part1.D6
  N7: LED2.cathode, R2.Pin_0
  N8: LED2.anode, Part1.D7

custom parts:
  LM393 Light Sensor: Digital Light sensor with LM393, Can be powered by 3.3V or 5V. Adjustable threshold through potentiometer
